// Logisim project Instruction Memory.circ as structural Verilog: 2 circuits, main circuit main
module main (
);

  wire clock_out;
  wire [31:0] instruction_memory_1_ir;

  Clock clock (.out(clock_out));
  Instruction_Memory instruction_memory_1 (.Clock_signal(clock_out), .enable(1'b1), .IR(instruction_memory_1_ir));
  Register #(.width(32)) IR (.D(instruction_memory_1_ir), .clk(clock_out));  // open: en, Q, clr
endmodule

// inst fetch
module Instruction_Memory (
  input  Clock_signal,
  input  enable,
  output [31:0] IR
);

  wire [31:0] adder_1_out, PC_q;

  Register #(.width(32)) PC (.D(adder_1_out), .Q(PC_q), .clk(Clock_signal));  // open: en, clr
  RAM #(.addrWidth(24), .dataWidth(32)) ram_1 (
    .addr(PC_q[23:0]), .data(IR), .clk(Clock_signal), .ld(enable));  // open: sel, clr
  Adder #(.width(32)) adder_1 (.a(PC_q), .b(32'h1), .out(adder_1_out));  // open: cin, cout
endmodule
